# Fritzing sketch MPU6050 (saved by Fritzing 1.0.4)
breadboards: 1

parts:
  A1 = Az-delivery ESP32 D1-Mini Nodemcu
  Part1 = InvenSense MPU6050

nets:
  N1: A1.Pin_1, A1.Pin_11
  N2: A1.Pin_2, A1.Pin_12
  N3: A1.Pin_3, A1.Pin_13
  N4: A1.Pin_4, A1.Pin_10, A1.Pin_14, A1.Pin_20, A1.Pin_21, A1.Pin_31, Part1.GND
  N5: A1.Pin_5, A1.Pin_15
  N6: A1.Pin_6, A1.Pin_16
  N7: A1.Pin_7, A1.Pin_17, Part1.SDA
  N8: A1.Pin_8, A1.Pin_18, Part1.SCL
  N9: A1.Pin_9, A1.Pin_19
  N10: A1.Pin_22, A1.Pin_32
  N11: A1.Pin_23, A1.Pin_33
  N12: A1.Pin_24, A1.Pin_34
  N13: A1.Pin_25, A1.Pin_35
  N14: A1.Pin_26, A1.Pin_36
  N15: A1.Pin_27, A1.Pin_37
  N16: A1.Pin_28, A1.Pin_38, Part1.VCC
  N17: A1.Pin_29, A1.Pin_39
  N18: A1.Pin_30, A1.Pin_40

custom parts:
  Az-delivery ESP32 D1-Mini Nodemcu: ESP32 D1 Mini Nodemcu WiFi Module + Bluetooth Internet Development Board.
